// Logisim project mips_processor.circ as structural Verilog: 5 circuits, main circuit registerfile_32
module registerfile_32 (
  input  reset,
  input  [31:0] \input ,
  input  load,
  input  [4:0] rs,
  input  [4:0] rd,
  input  [4:0] rt,
  output [31:0] rs_2,
  output [31:0] rt_2
);

  wire clock_1_out, demultiplexer_1_out0, demultiplexer_1_out1, demultiplexer_1_out2, demultiplexer_1_out3,
       demultiplexer_1_out4, demultiplexer_1_out5, demultiplexer_1_out6, demultiplexer_1_out7,
       demultiplexer_1_out8, demultiplexer_1_out9, demultiplexer_1_out10, demultiplexer_1_out11,
       demultiplexer_1_out12, demultiplexer_1_out13, demultiplexer_1_out14, demultiplexer_1_out15,
       demultiplexer_1_out16, demultiplexer_1_out17, demultiplexer_1_out18, demultiplexer_1_out19,
       demultiplexer_1_out20, demultiplexer_1_out21, demultiplexer_1_out22, demultiplexer_1_out23,
       demultiplexer_1_out24, demultiplexer_1_out25, demultiplexer_1_out26, demultiplexer_1_out27,
       demultiplexer_1_out28, demultiplexer_1_out29, demultiplexer_1_out30, demultiplexer_1_out31;
  wire [31:0] r0_zero_q, r1_at_q, r2_v0_q, r3_v1_q, r4_a0_q, r5_a1_q, r6_a2_q, r7_a3_q, r8_t0_q, r9_t1_q,
       r10_t2_q, r11_t3_q, r12_t4_q, r13_t5_q, r14_t6_q, r15_t7_q, r16_s0_q, r17_s1_q, r18_s2_q, r19_s3_q,
       r20_s4_q, r21_s5_q, r22_s6_q, r23_s7_q, r24_t8_q, r25_t9_q, r26_k0_q, r27_k1_q, r28_gp_q, r29_sp_q,
       r30_fp_q, r31_ra_q;

  Demultiplexer #(.select(5)) demultiplexer_1 (
    .out0(demultiplexer_1_out0), .out1(demultiplexer_1_out1), .out2(demultiplexer_1_out2),
    .out3(demultiplexer_1_out3), .out4(demultiplexer_1_out4), .out5(demultiplexer_1_out5),
    .out6(demultiplexer_1_out6), .out7(demultiplexer_1_out7), .out8(demultiplexer_1_out8),
    .out9(demultiplexer_1_out9), .out10(demultiplexer_1_out10), .out11(demultiplexer_1_out11),
    .out12(demultiplexer_1_out12), .out13(demultiplexer_1_out13), .out14(demultiplexer_1_out14),
    .out15(demultiplexer_1_out15), .out16(demultiplexer_1_out16), .out17(demultiplexer_1_out17),
    .out18(demultiplexer_1_out18), .out19(demultiplexer_1_out19), .out20(demultiplexer_1_out20),
    .out21(demultiplexer_1_out21), .out22(demultiplexer_1_out22), .out23(demultiplexer_1_out23),
    .out24(demultiplexer_1_out24), .out25(demultiplexer_1_out25), .out26(demultiplexer_1_out26),
    .out27(demultiplexer_1_out27), .out28(demultiplexer_1_out28), .out29(demultiplexer_1_out29),
    .out30(demultiplexer_1_out30), .out31(demultiplexer_1_out31), .in(load), .sel(rd));  // open: en
  Clock clock_1 (.out(clock_1_out));
  Register #(.width(32)) r0_zero (
    .D(\input ), .en(demultiplexer_1_out0), .Q(r0_zero_q), .clk(clock_1_out), .clr(reset));
  Register #(.width(32)) r1_at (.D(\input ), .en(demultiplexer_1_out1), .Q(r1_at_q), .clk(clock_1_out), .clr(reset));
  Register #(.width(32)) r2_v0 (.D(\input ), .en(demultiplexer_1_out2), .Q(r2_v0_q), .clk(clock_1_out), .clr(reset));
  Register #(.width(32)) r3_v1 (.D(\input ), .en(demultiplexer_1_out3), .Q(r3_v1_q), .clk(clock_1_out), .clr(reset));
  Register #(.width(32)) r4_a0 (.D(\input ), .en(demultiplexer_1_out4), .Q(r4_a0_q), .clk(clock_1_out), .clr(reset));
  Register #(.width(32)) r5_a1 (.D(\input ), .en(demultiplexer_1_out5), .Q(r5_a1_q), .clk(clock_1_out), .clr(reset));
  Register #(.width(32)) r6_a2 (.D(\input ), .en(demultiplexer_1_out6), .Q(r6_a2_q), .clk(clock_1_out), .clr(reset));
  Register #(.width(32)) r7_a3 (.D(\input ), .en(demultiplexer_1_out7), .Q(r7_a3_q), .clk(clock_1_out), .clr(reset));
  Register #(.width(32)) r8_t0 (.D(\input ), .en(demultiplexer_1_out8), .Q(r8_t0_q), .clk(clock_1_out), .clr(reset));
  Register #(.width(32)) r9_t1 (.D(\input ), .en(demultiplexer_1_out9), .Q(r9_t1_q), .clk(clock_1_out), .clr(reset));
  Register #(.width(32)) r10_t2 (.D(\input ), .en(demultiplexer_1_out10), .Q(r10_t2_q), .clk(clock_1_out), .clr(reset));
  Register #(.width(32)) r11_t3 (.D(\input ), .en(demultiplexer_1_out11), .Q(r11_t3_q), .clk(clock_1_out), .clr(reset));
  Register #(.width(32)) r12_t4 (.D(\input ), .en(demultiplexer_1_out12), .Q(r12_t4_q), .clk(clock_1_out), .clr(reset));
  Register #(.width(32)) r13_t5 (.D(\input ), .en(demultiplexer_1_out13), .Q(r13_t5_q), .clk(clock_1_out), .clr(reset));
  Register #(.width(32)) r14_t6 (.D(\input ), .en(demultiplexer_1_out14), .Q(r14_t6_q), .clk(clock_1_out), .clr(reset));
  Register #(.width(32)) r15_t7 (.D(\input ), .en(demultiplexer_1_out15), .Q(r15_t7_q), .clk(clock_1_out), .clr(reset));
  Register #(.width(32)) r16_s0 (.D(\input ), .en(demultiplexer_1_out16), .Q(r16_s0_q), .clk(clock_1_out), .clr(reset));
  Register #(.width(32)) r17_s1 (.D(\input ), .en(demultiplexer_1_out17), .Q(r17_s1_q), .clk(clock_1_out), .clr(reset));
  Register #(.width(32)) r18_s2 (.D(\input ), .en(demultiplexer_1_out18), .Q(r18_s2_q), .clk(clock_1_out), .clr(reset));
  Register #(.width(32)) r19_s3 (.D(\input ), .en(demultiplexer_1_out19), .Q(r19_s3_q), .clk(clock_1_out), .clr(reset));
  Register #(.width(32)) r20_s4 (.D(\input ), .en(demultiplexer_1_out20), .Q(r20_s4_q), .clk(clock_1_out), .clr(reset));
  Register #(.width(32)) r21_s5 (.D(\input ), .en(demultiplexer_1_out21), .Q(r21_s5_q), .clk(clock_1_out), .clr(reset));
  Register #(.width(32)) r22_s6 (.D(\input ), .en(demultiplexer_1_out22), .Q(r22_s6_q), .clk(clock_1_out), .clr(reset));
  Register #(.width(32)) r23_s7 (.D(\input ), .en(demultiplexer_1_out23), .Q(r23_s7_q), .clk(clock_1_out), .clr(reset));
  Register #(.width(32)) r24_t8 (.D(\input ), .en(demultiplexer_1_out24), .Q(r24_t8_q), .clk(clock_1_out), .clr(reset));
  Register #(.width(32)) r25_t9 (.D(\input ), .en(demultiplexer_1_out25), .Q(r25_t9_q), .clk(clock_1_out), .clr(reset));
  Register #(.width(32)) r26_k0 (.D(\input ), .en(demultiplexer_1_out26), .Q(r26_k0_q), .clk(clock_1_out), .clr(reset));
  Register #(.width(32)) r27_k1 (.D(\input ), .en(demultiplexer_1_out27), .Q(r27_k1_q), .clk(clock_1_out), .clr(reset));
  Register #(.width(32)) r28_gp (.D(\input ), .en(demultiplexer_1_out28), .Q(r28_gp_q), .clk(clock_1_out), .clr(reset));
  Register #(.width(32)) r29_sp (.D(\input ), .en(demultiplexer_1_out29), .Q(r29_sp_q), .clk(clock_1_out), .clr(reset));
  Register #(.width(32)) r30_fp (.D(\input ), .en(demultiplexer_1_out30), .Q(r30_fp_q), .clk(clock_1_out), .clr(reset));
  Register #(.width(32)) r31_ra (.D(\input ), .en(demultiplexer_1_out31), .Q(r31_ra_q), .clk(clock_1_out), .clr(reset));
  Multiplexer #(.select(5), .width(32)) multiplexer_1 (
    .in0(r0_zero_q), .in1(r1_at_q), .in2(r2_v0_q), .in3(r3_v1_q), .in4(r4_a0_q), .in5(r5_a1_q),
    .in6(r6_a2_q), .in7(r7_a3_q), .in8(r8_t0_q), .in9(r9_t1_q), .in10(r10_t2_q), .in11(r11_t3_q),
    .in12(r12_t4_q), .in13(r13_t5_q), .in14(r14_t6_q), .in15(r15_t7_q), .in16(r16_s0_q), .in17(r17_s1_q),
    .in18(r18_s2_q), .in19(r19_s3_q), .in20(r20_s4_q), .in21(r21_s5_q), .in22(r22_s6_q), .in23(r23_s7_q),
    .in24(r24_t8_q), .in25(r25_t9_q), .in26(r26_k0_q), .in27(r27_k1_q), .in28(r28_gp_q), .in29(r29_sp_q),
    .in30(r30_fp_q), .in31(r31_ra_q), .out(rs_2), .sel(rs));  // open: en
  Multiplexer #(.select(5), .width(32)) multiplexer_2 (
    .in0(r0_zero_q), .in1(r1_at_q), .in2(r2_v0_q), .in3(r3_v1_q), .in4(r4_a0_q), .in5(r5_a1_q),
    .in6(r6_a2_q), .in7(r7_a3_q), .in8(r8_t0_q), .in9(r9_t1_q), .in10(r10_t2_q), .in11(r11_t3_q),
    .in12(r12_t4_q), .in13(r13_t5_q), .in14(r14_t6_q), .in15(r15_t7_q), .in16(r16_s0_q), .in17(r17_s1_q),
    .in18(r18_s2_q), .in19(r19_s3_q), .in20(r20_s4_q), .in21(r21_s5_q), .in22(r22_s6_q), .in23(r23_s7_q),
    .in24(r24_t8_q), .in25(r25_t9_q), .in26(r26_k0_q), .in27(r27_k1_q), .in28(r28_gp_q), .in29(r29_sp_q),
    .in30(r30_fp_q), .in31(r31_ra_q), .out(rt_2), .sel(rt));  // open: en
endmodule

module control (
  input  [5:0] opcode,
  input  [5:0] func,
  output Bne,
  output [1:0] RegDst,
  output ALUSrc,
  output [1:0] RegToMem,
  output beq,
  output RegWrite,
  output MemRead,
  output MemWrite,
  output Jump,
  output [3:0] ALUfunc,
  output jr,
  output slt
);

  wire nor_1_out;
  wire [3:0] rom_2_data;
  wire [14:11] rom_1_data;

  ROM #(.addrWidth(6), .dataWidth(15)) rom_1 (
    .addr(opcode), .data({rom_1_data, Jump, MemWrite, MemRead, RegWrite, beq, RegToMem, ALUSrc, RegDst, Bne}));  // open: sel
  ROM #(.addrWidth(6), .dataWidth(4)) rom_2 (.addr(func), .data(rom_2_data));  // open: sel
  nor nor_1 (nor_1_out, opcode[0], opcode[1], opcode[2], opcode[3], opcode[4], opcode[5]);
  Comparator #(.width(12)) comparator_1 (.a({opcode, func}), .b(12'h8), .eq(jr));  // open: gt, lt
  Comparator #(.width(12)) comparator_2 (.a({opcode, func}), .b(12'h2a), .eq(slt));  // open: gt, lt
  Multiplexer #(.width(4)) multiplexer_1 (
    .in0(rom_1_data), .in1(rom_2_data), .out(ALUfunc), .sel(nor_1_out));  // open: en

  // Notes on the sheet:
  //   contents of rom_1 (hex, n*v repeats v):
  //   80 0 400 4a4 40 1 0 0 8a 0 58ba 24*0 19a 6*0 b0 208
  //   contents of rom_2 (hex, n*v repeats v):
  //   8 7*0 9 25*0 1 0 4 0 7 0 0 0 b
endmodule

module InstructionFetch (
  input  [31:0] offset,
  input  zero,
  input  jump,
  input  jr,
  input  rest,
  input  [31:0] jr_add,
  input  [25:0] address,
  output [31:0] pc_4,
  output [31:0] out_9
);

  wire clock_1_out;
  wire [31:0] adder_2_out, multiplexer_1_out, multiplexer_2_out, multiplexer_3_out, register_1_q,
       shifter_1_out;

  Clock clock_1 (.out(clock_1_out));
  Register #(.width(32)) register_1 (
    .D(multiplexer_3_out), .Q(register_1_q), .clk(clock_1_out), .clr(rest));  // open: en
  Adder #(.width(32)) adder_1 (.a(register_1_q), .b(32'h4), .out(pc_4));  // open: cin, cout
  ROM #(.addrWidth(10), .dataWidth(32)) rom_1 (.addr(register_1_q[11:2]), .data(out_9));  // open: sel
  Shifter #(.width(32)) shifter_1 (.in(offset), .\dist (5'b00010), .out(shifter_1_out));
  Adder #(.width(32)) adder_2 (.a(pc_4), .b(shifter_1_out), .out(adder_2_out));  // open: cin, cout
  Multiplexer #(.width(32)) multiplexer_1 (
    .in0(pc_4), .in1(adder_2_out), .out(multiplexer_1_out), .sel(zero));  // open: en
  Multiplexer #(.width(32)) multiplexer_2 (
    .in0(multiplexer_1_out), .in1({pc_4[31:28], address, 2'b00}), .out(multiplexer_2_out), .sel(jump));  // open: en
  Multiplexer #(.width(32)) multiplexer_3 (
    .in0(multiplexer_2_out), .in1(jr_add), .out(multiplexer_3_out), .sel(jr));  // open: en

  // Notes on the sheet:
  //   contents of rom_1 (hex, n*v repeats v):
  //   20010000 20090003 ac290000 200a0009 ac2a0004 200b0001 ac2b0008 200c0005 ac2c000c 200d0006 ac2d0010
  //   200e0007 ac2e0014 2020 20050006 c01001b 0 8010044 0 54880 894820 8d280000 8d2a0004 ad2a0000 ad280004
  //   3e00008 0 23bdffec afbf0010 afb3000c afb20008 afb10004 afb00000 49020 59820 8020 213402a 10080017 0
  //   2211ffff 2a280000 1408000f 0 114880 2495020 8d4b0000 8d4c0004 18b402a 10080008 0 122020 112820
  //   c010013 0 2231ffff 8010028 0 22100001 8010024 0 8fb00000 8fb10004 8fb20008 8fb3000c 8fbf0010
  //   23bd0014 3e00008
endmodule

module MIPS (
  input  reset
);

  wire alu_1_zero, and_1_out, and_2_out, clock_1_out, control_1_alusrc, control_1_beq, control_1_bne,
       control_1_jr, control_1_jump, control_1_memread, control_1_memwrite, control_1_regwrite,
       control_1_slt, not_1_out, or_1_out;
  wire [1:0] control_1_regdst, control_1_regtomem;
  wire [3:0] control_1_alufunc;
  wire [4:0] multiplexer_1_out;
  wire [31:0] alu_1_output, alu_1_slti, bit_extender_1_out, instructionfetch_1_out_9,
       instructionfetch_1_pc_4, multiplexer_2_out, multiplexer_3_out, multiplexer_4_out, ram_1_data,
       registerfile_32_1_rs_2, registerfile_32_1_rt_2;

  and and_1 (and_1_out, alu_1_zero, control_1_beq);
  and and_2 (and_2_out, not_1_out, control_1_bne);
  or or_1 (or_1_out, and_1_out, and_2_out);
  InstructionFetch instructionfetch_1 (
    .offset(bit_extender_1_out), .zero(or_1_out), .jump(control_1_jump), .rest(reset),
    .address(instructionfetch_1_out_9[25:0]), .out_9(instructionfetch_1_out_9),
    .pc_4(instructionfetch_1_pc_4), .jr_add(registerfile_32_1_rs_2), .jr(control_1_jr));
  control control_1 (
    .opcode(instructionfetch_1_out_9[31:26]), .func(instructionfetch_1_out_9[5:0]),
    .RegDst(control_1_regdst), .ALUSrc(control_1_alusrc), .RegToMem(control_1_regtomem), .beq(control_1_beq),
    .RegWrite(control_1_regwrite), .MemRead(control_1_memread), .MemWrite(control_1_memwrite),
    .Jump(control_1_jump), .ALUfunc(control_1_alufunc), .Bne(control_1_bne), .jr(control_1_jr),
    .slt(control_1_slt));
  Multiplexer #(.select(2), .width(5)) multiplexer_1 (
    .in0(instructionfetch_1_out_9[15:11]), .in1(instructionfetch_1_out_9[20:16]), .in2({5{1'b1}}),
    .out(multiplexer_1_out), .sel(control_1_regdst));  // open: in3, en
  assign bit_extender_1_out = {{16{instructionfetch_1_out_9[15]}}, instructionfetch_1_out_9[15:0]};  // Bit_Extender bit_extender_1
  Multiplexer #(.width(32)) multiplexer_2 (
    .in0(multiplexer_4_out), .in1(alu_1_slti), .out(multiplexer_2_out), .sel(control_1_slt));  // open: en
  registerfile_32 registerfile_32_1 (
    .reset(reset), .\input (multiplexer_2_out), .load(control_1_regwrite),
    .rs(instructionfetch_1_out_9[25:21]), .rd(multiplexer_1_out), .rt(instructionfetch_1_out_9[20:16]),
    .rs_2(registerfile_32_1_rs_2), .rt_2(registerfile_32_1_rt_2));
  Multiplexer #(.width(32)) multiplexer_3 (
    .in0(registerfile_32_1_rt_2), .in1(bit_extender_1_out), .out(multiplexer_3_out), .sel(control_1_alusrc));  // open: en
  not not_1 (not_1_out, alu_1_zero);
  Multiplexer #(.select(2), .width(32)) multiplexer_4 (
    .in0(alu_1_output), .in1(ram_1_data), .in2(instructionfetch_1_pc_4), .in3(alu_1_output),
    .out(multiplexer_4_out), .sel(control_1_regtomem));  // open: en
  ALU alu_1 (
    .rs(registerfile_32_1_rs_2), .rt(multiplexer_3_out), .shiftbit(instructionfetch_1_out_9[10:6]),
    .ALUfunc(control_1_alufunc), .zero(alu_1_zero), .slti(alu_1_slti), .\output (alu_1_output));
  Clock clock_1 (.out(clock_1_out));
  RAM #(.addrWidth(12), .dataWidth(32), .bus("separate")) ram_1 (
    .addr(alu_1_output[13:2]), .din(registerfile_32_1_rt_2), .data(ram_1_data), .str(control_1_memwrite),
    .clk(clock_1_out), .ld(control_1_memread), .clr(reset));  // open: sel
endmodule

module ALU (
  input  [31:0] rs,
  input  [31:0] rt,
  input  [4:0] shiftbit,
  input  [3:0] ALUfunc,
  output zero,
  output [31:0] slti,
  output [31:0] \output 
);

  wire comparator_1_lt, comparator_2_lt;
  wire [31:0] adder_1_out, and_1_out, bit_extender_1_out, divider_1_out, multiplier_1_out, nor_1_out,
       or_1_out, shifter_1_out, shifter_2_out, shifter_3_out, subtractor_1_out, xor_1_out;

  Comparator #(.width(32)) comparator_1 (.a(rs), .b(rt), .lt(comparator_1_lt));  // open: gt, eq
  Comparator #(.width(32)) comparator_2 (.a(rs), .b(rt), .eq(zero), .lt(comparator_2_lt));  // open: gt
  Adder #(.width(32)) adder_1 (.a(rs), .b(rt), .out(adder_1_out));  // open: cin, cout
  Subtractor #(.width(32)) subtractor_1 (.a(rs), .b(rt), .out(subtractor_1_out));  // open: bin, bout
  Multiplier #(.width(32)) multiplier_1 (.a(rs), .b(rt), .out(multiplier_1_out));  // open: cin, cout
  Divider #(.width(32)) divider_1 (.a(rs), .b(rt), .out(divider_1_out));  // open: upper, rem
  assign and_1_out = rs & rt;  // AND_Gate and_1, 32 bits wide
  assign or_1_out = rs | rt;  // OR_Gate or_1, 32 bits wide
  assign nor_1_out = ~(rs | rt);  // NOR_Gate nor_1, 32 bits wide
  assign xor_1_out = rs ^ rt;  // XOR_Gate xor_1, 32 bits wide
  Shifter #(.width(32)) shifter_1 (.in(rt), .\dist (shiftbit), .out(shifter_1_out));
  Shifter #(.width(32), .shift("lr")) shifter_2 (.in(rt), .\dist (shiftbit), .out(shifter_2_out));
  Shifter #(.width(32), .shift("ar")) shifter_3 (.in(rt), .\dist (shiftbit), .out(shifter_3_out));
  assign bit_extender_1_out = {{31{1'b0}}, comparator_1_lt};  // Bit_Extender bit_extender_1
  assign slti = {{31{1'b0}}, comparator_2_lt};  // Bit_Extender bit_extender_2
  Multiplexer #(.select(4), .width(32)) multiplexer_1 (
    .in0(adder_1_out), .in1(subtractor_1_out), .in2(multiplier_1_out), .in3(divider_1_out), .in4(and_1_out),
    .in5(or_1_out), .in6(nor_1_out), .in7(xor_1_out), .in8(shifter_1_out), .in9(shifter_2_out),
    .in10(shifter_3_out), .in11(bit_extender_1_out), .out(\output ), .sel(ALUfunc));  // open: in12, in13, in14, in15, en
endmodule
